// Logisim project Logisim 2 2-bit adder.circ as structural Verilog: 1 circuit, main circuit main
module main (
  input  C_in,
  input  [1:0] A0__A1,
  input  [1:0] A2__A3,
  input  [1:0] B2__B3,
  input  [1:0] B0__B1,
  output [1:0] out_6,
  output [1:0] out_7,
  output C_out
);

  wire adder_1_cout;

  Adder #(.width(2)) adder_1 (.a(A0__A1), .b(B2__B3), .out(out_7), .cin(C_in), .cout(adder_1_cout));
  Adder #(.width(2)) adder_2 (.a(A2__A3), .b(B0__B1), .out(out_6), .cin(adder_1_cout), .cout(C_out));
endmodule
