// Logisim project Logisim 4 1-bit full adder.circ as structural Verilog: 1 circuit, main circuit main
module main (
  input  Cin,
  input  [3:0] A0,
  input  [3:0] B0,
  output [3:0] S0,
  output C_out
);

  Adder #(.width(4)) adder_1 (.a(A0), .b(B0), .out(S0), .cin(Cin), .cout(C_out));
endmodule
