// Logisim project logisim 1 4-bit adder.circ as structural Verilog: 1 circuit, main circuit main
module main (
  input  C_in,
  input  A3,
  input  A2,
  input  A1,
  input  A0,
  input  B3,
  input  B2,
  input  B1,
  input  B0,
  output C3,
  output C2,
  output C1,
  output C0,
  output C_out
);

  wire adder_1_cout, adder_2_cout, adder_3_cout;

  Adder #(.width(1)) adder_1 (.a(A3), .b(B3), .out(C3), .cin(C_in), .cout(adder_1_cout));
  Adder #(.width(1)) adder_2 (.a(A2), .b(B2), .out(C2), .cin(adder_1_cout), .cout(adder_2_cout));
  Adder #(.width(1)) adder_3 (.a(A1), .b(B1), .out(C1), .cin(adder_2_cout), .cout(adder_3_cout));
  Adder #(.width(1)) adder_4 (.a(A0), .b(B0), .out(C0), .cin(adder_3_cout), .cout(C_out));
endmodule
