// Logisim project logisim full adder 1.circ as structural Verilog: 1 circuit, main circuit main
module main (
  input  A,
  input  B,
  input  C_in,
  output SUM,
  output CARRY
);

  wire and_1_out, and_2_out, xor_1_out;

  xor xor_1 (xor_1_out, A, B);
  and and_1 (and_1_out, A, B);
  and and_2 (and_2_out, xor_1_out, C_in);
  xor xor_2 (SUM, xor_1_out, C_in);
  or or_1 (CARRY, and_2_out, and_1_out);
endmodule
