// Logisim project Logisim experiment 1 function1.circ as structural Verilog: 1 circuit, main circuit main
module main (
  input  A,
  input  B,
  input  C,
  output X
);

  wire and_1_out, and_2_out, not_1_out;

  not not_1 (not_1_out, B);
  and and_1 (and_1_out, A, C);
  and and_2 (and_2_out, not_1_out, C);
  or or_1 (X, and_1_out, and_2_out);

  // Notes on the sheet:
  //   AC
  //   B' C
  //   AC + B'C
endmodule
