// Logisim project Logisim experiment 2.circ as structural Verilog: 1 circuit, main circuit main
module main (
  input  a,
  input  b,
  input  c,
  input  d,
  output x
);

  wire and_1_out, and_2_out, and_3_out, and_4_out, and_5_out, and_6_out, not_1_out, not_2_out, not_3_out,
       not_4_out, not_5_out, not_6_out, not_7_out, not_8_out;

  not not_1 (not_1_out, c);
  not not_2 (not_2_out, a);
  not not_3 (not_3_out, d);
  not not_4 (not_4_out, b);
  not not_5 (not_5_out, c);
  not not_6 (not_6_out, d);
  and and_1 (and_1_out, a, b, not_1_out, d);
  and and_2 (and_2_out, not_2_out, b, c, not_3_out);
  and and_3 (and_3_out, a, d, c);
  and and_4 (and_4_out, a, not_4_out, not_5_out, not_6_out);
  and and_5 (and_5_out, a, b, not_7_out);
  not not_7 (not_7_out, d);
  not not_8 (not_8_out, b);
  and and_6 (and_6_out, a, not_8_out, c);
  or or_1 (x, and_1_out, and_2_out, and_3_out, and_4_out, and_5_out, and_6_out);
endmodule
