// Logisim project logisim experiment 1 function 2 .circ as structural Verilog: 1 circuit, main circuit main
module main (
  input  A,
  input  B,
  input  C,
  output C_prime__B_prime_A__B_prime
);

  wire and_1_out, not_1_out, not_2_out, not_3_out, or_1_out;

  not not_1 (not_1_out, C);
  not not_2 (not_2_out, B);
  and and_1 (and_1_out, not_2_out, A);
  or or_1 (or_1_out, not_1_out, and_1_out);
  not not_3 (not_3_out, B);
  and and_2 (C_prime__B_prime_A__B_prime, or_1_out, not_3_out);

  // Notes on the sheet:
  //   C'
  //   B'
  //   A
  //   B'A
  //   C' + B'C
  //   B'
endmodule
